# Fritzing sketch RangeSensorBBProto (saved by Fritzing 0.9.2b)
circuit board: 3.86363cm x 5.82807cm
breadboards: 3
perfboards: 1

parts:
  Nano_v3 = Arduino Nano (Rev3.0)
  RangeSensor = Parallax Ping))) Ultrasonic Range Sendor [part_number=28014]
  Mode = SWITCH_SPDT [package=kps-1290]
  Max_Range = POT [package=alps_pot]
  R3 = Resistor [tolerance=±5% resistance=10k package=THT]
  Distance = LED - 3mm [color="Green (555nm)" package="3 mm [THT]"]
  R4 = Resistor [tolerance=±5% resistance=1k package=THT]
  C1 = Ceramic Capacitor [capacitance=0.1µF package="0603 [SMD, multilayer]"]
  RangeSensor1 = Parallax Ping))) Ultrasonic Range Sendor [part_number=28014]
  Distance1 = LED - 3mm [color="Green (555nm)" package="3 mm [THT]"]
  Mode1 = SWITCH_SPDT [package=kps-1290]
  Max_Range1 = POT [package=alps_pot]
  R5 = Resistor [tolerance=±5% resistance=10k package=THT]
  R6 = Resistor [tolerance=±5% resistance=1k package=THT]
  C2 = Ceramic Capacitor [capacitance=0.1µF package="0603 [SMD, multilayer]"]

nets:
  GND: Nano_v3.GND, RangeSensor.GND, Max_Range.A, Distance.cathode, R4.Pin_1, C1.1
  N1: Nano_v3.D2, RangeSensor.Sig
  N2: Nano_v3.D3, Mode.S, R4.Pin_0
  N3: Nano_v3.D6, R3.Pin_0, R3.Pin_1, Distance.anode, C1.0
  5V: Nano_v3.5V, RangeSensor.5V, Mode.P, Max_Range.E
  N4: Nano_v3.A0, Max_Range.S
  N5: RangeSensor1.5V, Mode1.P, Max_Range1.E
  N6: RangeSensor1.GND, Distance1.cathode, Max_Range1.A, R6.Pin_1, C2.1
  N7: Distance1.anode, R5.Pin_0, R5.Pin_1, C2.0
  N8: Mode1.S, R6.Pin_0

notes:
  Out to SIG IN on LittleBit

// code stored in the sketch: RangeSensor.ino
/* Ping))) Sensor

   This sketch reads a PING))) ultrasonic rangefinder and returns the
   distance to the closest object in range. To do this, it sends a pulse
   to the sensor to initiate a reading, then listens for a pulse
   to return.  The length of the returning pulse is proportional to
   the distance of the object from the sensor.

   The circuit:
	* +V connection of the PING))) attached to +5V
	* GND connection of the PING))) attached to ground
	* SIG connection of the PING))) attached to digital pin 2

   http://www.arduino.cc/en/Tutorial/Ping

   created 3 Nov 2008
   by David A. Mellis
   modified 06 Aug 2011
   by Tom Igoe
	 modified 22 Jun 2015
   by Shai Perednik shaiss@gmail.com

   This example code is in the public domain.

 */


// this constant won't change.  It's the pin number
// of the sensor's output:
const int pingPin = 2; //Sig pin of the Ping))) Sensor
const int ledPin = 6; //The pin the LED is attached to
float brightness = 0; //set the initial value to null

void setup() {
  // initialize serial communication:
  Serial.begin(9600);
	pinMode(ledPin, OUTPUT);  //declare ledPin as an output
}

void loop()
{
  // establish variables for duration of the ping,
  // and the distance result in inches and centimeters:
  long duration, inches, cm;

  // The PING))) is triggered by a HIGH pulse of 2 or more microseconds.
  // Give a short LOW pulse beforehand to ensure a clean HIGH pulse:
  pinMode(pingPin, OUTPUT);
  digitalWrite(pingPin, LOW);
  delayMicroseconds(2);
  digitalWrite(pingPin, HIGH);
  delayMicroseconds(5);
  digitalWrite(pingPin, LOW);

  // The same pin is used to read the signal from the PING))): a HIGH  
  // pulse whose duration is the time (in microseconds) from the sending
  // of the ping to the reception of its echo off of an object.
  pinMode(pingPin, INPUT);
  duration = pulseIn(pingPin, HIGH);

  // convert the time into a distance
  inches = microsecondsToInches(duration);
  cm = microsecondsToCentimeters(duration);

  //Serial.print(inches);
  //Serial.print("in, ");
  Serial.print(cm);
  //Serial.print("cm");
  Serial.println();

	//convert distance of object to brightness.  
	//Ping))) range is 2cm - 3M/.78in - 118.11in
	//brightness = 144/300.00;
	//brightness = ((((cm/300.00)*255)-255)*-1);  //closer == brighter.  If cm =0 returns 255.
 //Serial.println(brightness);
	brightness = ((cm/300.00))*255; //farther == brighter.  If cm = 300 returns 255
	
	//write distance to LED
	analogWrite(ledPin, brightness);

	//delay to get a fading effect
	delay(50);
}

long microsecondsToInches(long microseconds)
{
  // According to Parallax's datasheet for the PING))), there are
  // 73.746 microseconds per inch (i.e. sound travels at 1130 feet per
  // second).  This gives the distance travelled by the ping, outbound
  // and return, so we divide by 2 to get the distance of the obstacle.
  // See: http://www.parallax.com/dl/docs/prod/acc/28015-PING-v1.3.pdf
  return microseconds / 74 / 2;
}

long microsecondsToCentimeters(long microseconds)
{
  // The speed of sound is 340 m/s or 29 microseconds per centimeter.
  // The ping travels out and back, so to find the distance of the
  // object we take half of the distance travelled.
  return microseconds / 29 / 2;
}

// code stored in the sketch: RangeSensorWLCD.ino
/* Ping))) Sensor

   This sketch reads a PING))) ultrasonic rangefinder and returns the
   distance to the closest object in range. To do this, it sends a pulse
   to the sensor to initiate a reading, then listens for a pulse
   to return.  The length of the returning pulse is proportional to
   the distance of the object from the sensor.

   The circuit:
	* +V connection of the PING))) attached to +5V
	* GND connection of the PING))) attached to ground
	* SIG connection of the PING))) attached to digital pin 2

   http://www.arduino.cc/en/Tutorial/Ping

   created 3 Nov 2008
   by David A. Mellis
   modified 06 Aug 2011
   by Tom Igoe
	 modified 22 Jun 2015
   by Shai Perednik shaiss@gmail.com

   This example code is in the public domain.

 */

#include <TFT.h>  // Arduino LCD library
#include <SPI.h>

// this constant won't change.  It's the pin number
// of the sensor's output:
const int pingPin = 2;

// pin definition for the Uno
#define cs   10
#define dc   9
#define rst  8

// create an instance of the library
TFT TFTscreen = TFT(cs, dc, rst);

// char array to print to the screen
char sensorPrintout[6];

void setup() {
  // initialize serial communication:
  Serial.begin(9600);
  
    // Put this line at the beginning of every sketch that uses the GLCD:
  TFTscreen.begin();

  // clear the screen with a black background
  TFTscreen.background(0, 0, 0);

  // write the static text to the screen
  // set the font color to white
  TFTscreen.stroke(255, 255, 255);
  // set the font size
  TFTscreen.setTextSize(2);
  // write the text to the top left corner of the screen
  TFTscreen.text("Sensor Value :\n ", 0, 0);
  // ste the font size very large for the loop
  TFTscreen.setTextSize(5);
  TFTscreen.text("in", 0, 60);
}

void loop()
{
  // establish variables for duration of the ping,
  // and the distance result in inches and centimeters:
  long duration, inches, cm;

  // The PING))) is triggered by a HIGH pulse of 2 or more microseconds.
  // Give a short LOW pulse beforehand to ensure a clean HIGH pulse:
  pinMode(pingPin, OUTPUT);
  digitalWrite(pingPin, LOW);
  delayMicroseconds(2);
  digitalWrite(pingPin, HIGH);
  delayMicroseconds(5);
  digitalWrite(pingPin, LOW);

  // The same pin is used to read the signal from the PING))): a HIGH  
  // pulse whose duration is the time (in microseconds) from the sending
  // of the ping to the reception of its echo off of an object.
  pinMode(pingPin, INPUT);
  duration = pulseIn(pingPin, HIGH);

  // convert the time into a distance
  inches = microsecondsToInches(duration);
  cm = microsecondsToCentimeters(duration);

  Serial.print(inches);
  Serial.print("in, ");
  Serial.print(cm);
  Serial.print("cm");
  Serial.println();

  String sensorVal = String(inches);
  //sensorVal += " in";
  sensorVal.toCharArray(sensorPrintout, 6);
  
  
  // set the font color
  TFTscreen.stroke(255, 255, 255);
  // print the sensor value
  TFTscreen.text(sensorPrintout, 0, 20);
  // wait for a moment
  delay(100);
  // erase the text you just wrote
  TFTscreen.stroke(0, 0, 0);
  TFTscreen.text(sensorPrintout, 0, 20);
}

long microsecondsToInches(long microseconds)
{
  // According to Parallax's datasheet for the PING))), there are
  // 73.746 microseconds per inch (i.e. sound travels at 1130 feet per
  // second).  This gives the distance travelled by the ping, outbound
  // and return, so we divide by 2 to get the distance of the obstacle.
  // See: http://www.parallax.com/dl/docs/prod/acc/28015-PING-v1.3.pdf
  return microseconds / 74 / 2;
}

long microsecondsToCentimeters(long microseconds)
{
  // The speed of sound is 340 m/s or 29 microseconds per centimeter.
  // The ping travels out and back, so to find the distance of the
  // object we take half of the distance travelled.
  return microseconds / 29 / 2;
}
